// Logisim project gryu2project1.circ as structural Verilog: 2 circuits, main circuit main
module main (
  output Clock,
  output State,
  output R1,
  output Y1,
  output G1,
  output R2,
  output Y2,
  output halt,
  output G2
);

  wire Clock_out;
  wire [6:1] counter_1_q;

  Clock u_Clock (.out(Clock_out));
  Counter #(.width(7), .max('h7f)) counter_1 (
    .Q({counter_1_q[6:4], State, counter_1_q[2:1], Clock}), .carry(halt), .clk(Clock_out));  // open: load, D, count, clr
  Traffic_Light traffic_light_1 (.State(State), .Clock(Clock), .R1(R1), .Y1(Y1), .G1(G1), .R2(R2), .Y2(Y2), .G2(G2));
endmodule

module Traffic_Light (
  input  State,
  input  Clock,
  output R1,
  output Y1,
  output G1,
  output R2,
  output Y2,
  output G2
);

  wire and_1_out, and_2_out, and_3_out, and_4_out, and_5_out, and_6_out, and_7_out, and_8_out, and_9_out,
       and_10_out, d_ff_1_q, d_ff_2_q, d_ff_3_q, not_1_out, or_2_out, or_3_out, or_4_out, or_5_out, or_6_out,
       or_10_out, or_11_out, S1_q, S2_q, S3_q;

  or or_1 (R1, or_2_out, or_6_out);
  or or_2 (or_2_out, and_1_out, and_2_out, and_3_out, and_6_out);
  and and_1 (and_1_out, State, ~S1_q, ~S2_q, ~S3_q);  // AND_Gate
  or or_3 (or_3_out, and_8_out, and_5_out, and_4_out);
  or or_4 (or_4_out, and_3_out, and_9_out, and_2_out);
  or or_5 (or_5_out, and_5_out, and_3_out, and_10_out, and_1_out);
  or or_6 (or_6_out, and_9_out, and_10_out);
  or or_7 (Y1, and_5_out, and_7_out);
  and and_2 (and_2_out, State, ~S1_q, ~S2_q, S3_q);  // AND_Gate
  D_Flip_Flop d_ff_1 (.clk(Clock), .D(or_3_out), .Q(d_ff_1_q));  // open: Qn, preset, en, reset
  D_Flip_Flop d_ff_2 (.clk(Clock), .D(or_4_out), .Q(d_ff_2_q));  // open: Qn, preset, en, reset
  D_Flip_Flop d_ff_3 (.clk(Clock), .D(or_5_out), .Q(d_ff_3_q));  // open: Qn, preset, en, reset
  not not_1 (not_1_out, Clock);
  or or_8 (G1, and_4_out, and_8_out);
  and and_3 (and_3_out, State, ~S1_q, S2_q, ~S3_q);  // AND_Gate
  D_Flip_Flop S1 (.clk(not_1_out), .D(d_ff_1_q), .Q(S1_q));  // open: Qn, preset, en, reset
  D_Flip_Flop S2 (.clk(not_1_out), .D(d_ff_2_q), .Q(S2_q));  // open: Qn, preset, en, reset
  D_Flip_Flop S3 (.clk(not_1_out), .D(d_ff_3_q), .Q(S3_q));  // open: Qn, preset, en, reset
  or or_9 (R2, or_10_out, or_11_out);
  or or_10 (or_10_out, and_3_out, and_4_out, and_5_out, and_6_out);
  and and_4 (and_4_out, State, ~S1_q, S2_q, S3_q);  // AND_Gate
  or or_11 (or_11_out, and_7_out, and_8_out);
  or or_12 (Y2, and_2_out, and_9_out);
  and and_5 (and_5_out, State, S1_q, ~S2_q, ~S3_q);  // AND_Gate
  or or_13 (G2, and_1_out, and_10_out);
  and and_6 (and_6_out, State, S1_q, ~S2_q, S3_q);  // AND_Gate
  and and_7 (and_7_out, ~S3_q, ~S2_q, S1_q);  // AND_Gate
  and and_8 (and_8_out, S3_q, S2_q, ~S1_q);  // AND_Gate
  and and_9 (and_9_out, S3_q, ~S2_q, ~S1_q);  // AND_Gate
  and and_10 (and_10_out, ~S3_q, ~S2_q, ~S1_q);  // AND_Gate
endmodule
